// Logisim project .Arch_EVM222.circ as structural Verilog
module HalfAdder (
  input  a,
  input  b,
  output s,
  output carry
);

  and and_1 (carry, a, b);
  xor xor_1 (s, a, b);
endmodule

module FullAdder (
  input  Cin,
  input  a,
  input  b,
  output s,
  output Cout
);

  wire halfadder_1_carry, halfadder_1_s, halfadder_2_carry;

  HalfAdder halfadder_1 (.a(a), .b(b), .s(halfadder_1_s), .carry(halfadder_1_carry));
  HalfAdder halfadder_2 (.a(Cin), .b(halfadder_1_s), .s(s), .carry(halfadder_2_carry));
  or or_1 (Cout, halfadder_2_carry, halfadder_1_carry);
endmodule

module CPA (
  input  Cin,
  input  [3:0] a,
  input  [3:0] b,
  output [3:0] S,
  output Cout
);

  wire fulladder_1_cout, fulladder_2_cout, fulladder_3_cout;

  FullAdder fulladder_1 (.Cin(Cin), .a(a[0]), .b(b[0]), .s(S[0]), .Cout(fulladder_1_cout));
  FullAdder fulladder_2 (.Cin(fulladder_1_cout), .a(a[1]), .b(b[1]), .s(S[1]), .Cout(fulladder_2_cout));
  FullAdder fulladder_3 (.Cin(fulladder_2_cout), .a(a[2]), .b(b[2]), .s(S[2]), .Cout(fulladder_3_cout));
  FullAdder fulladder_4 (.Cin(fulladder_3_cout), .a(a[3]), .b(b[3]), .s(S[3]), .Cout(Cout));
endmodule

module Incrementer (
  input  Cin,
  input  [3:0] a,
  output [3:0] out_3
);

  CPA cpa_1 (.Cin(Cin), .a(a), .b(4'b0001), .S(out_3));  // open: Cout
endmodule

module Sub (
  input  Cin,
  input  [3:0] a,
  input  [3:0] b,
  output [3:0] S,
  output Cout
);

  wire [3:0] not_1_out;

  assign not_1_out = ~b;  // NOT_Gate not_1, 4 bits wide
  CPA cpa_1 (.Cin(Cin), .a(a), .b(not_1_out), .S(S), .Cout(Cout));
endmodule

module SubSum (
  input  K,
  input  [3:0] b,
  input  [3:0] a,
  output Cout,
  output [3:0] S
);

  wire [3:0] multiplexer_1_out, not_1_out;

  assign not_1_out = ~b;  // NOT_Gate not_1, 4 bits wide
  Multiplexer #(.width(4)) multiplexer_1 (.in0(b), .in1(not_1_out), .out(multiplexer_1_out), .sel(K));
  CPA cpa_1 (.Cin(K), .a(multiplexer_1_out), .b(a), .S(S), .Cout(Cout));
endmodule

module OverFlow (
  input  K,
  input  [3:0] b,
  input  [3:0] a,
  output V,
  output [3:0] S
);

  wire xnor_1_out, xor_1_out;
  wire [3:0] multiplexer_1_out, not_1_out;

  assign not_1_out = ~b;  // NOT_Gate not_1, 4 bits wide
  Multiplexer #(.width(4)) multiplexer_1 (.in0(b), .in1(not_1_out), .out(multiplexer_1_out), .sel(K));
  CPA cpa_1 (.Cin(K), .a(multiplexer_1_out), .b(a), .S(S));  // open: Cout
  xnor xnor_1 (xnor_1_out, multiplexer_1_out[3], a[3]);
  xor xor_1 (xor_1_out, a[3], S[3]);
  and and_1 (V, xnor_1_out, xor_1_out);
endmodule

module Comparators (
  input  [3:0] a,
  input  [3:0] b,
  output Equal
);

  wire and_1_out, and_2_out, xnor_1_out, xnor_2_out, xnor_3_out, xnor_4_out;

  xnor xnor_1 (xnor_1_out, a[0], b[0]);
  xnor xnor_2 (xnor_2_out, a[1], b[1]);
  xnor xnor_3 (xnor_3_out, a[2], b[2]);
  xnor xnor_4 (xnor_4_out, a[3], b[3]);
  and and_1 (and_1_out, xnor_3_out, xnor_4_out);
  and and_2 (and_2_out, xnor_1_out, xnor_2_out);
  and and_3 (Equal, and_2_out, and_1_out);
endmodule

module Comparators2 (
  input  [3:0] a,
  input  [3:0] b,
  output out_3
);

  wire not_1_out;
  wire [3:0] sub_1_s;

  Sub sub_1 (.Cin(1'b1), .a(b), .b(a), .S(sub_1_s));  // open: Cout
  not not_1 (not_1_out, sub_1_s[0]);
  and and_1 (out_3, not_1_out, 1'b1);
endmodule

module SintComp (
  input  [3:0] a,
  input  [3:0] b,
  output neq,
  output eq,
  output lte,
  output gt,
  output gte,
  output lt
);

  Comparators comparators_1 (.a(a), .b(b), .Equal(eq));
  Comparators2 comparators2_1 (.a(a), .b(b), .out_3(gt));
  Comparators2 comparators2_2 (.a(a), .b(b), .out_3(lt));
  not not_1 (neq, eq);
  not not_2 (lte, gt);
  not not_3 (gte, lt);
endmodule

module ALU (
  input  [2:0] ALUControl,
  input  [31:0] B,
  input  [31:0] A
);

  wire [31:0] multiplexer_1_out, not_1_out;

  Multiplexer #(.width(32)) multiplexer_1 (.in0(B), .in1(not_1_out), .out(multiplexer_1_out), .sel(ALUControl[0]));
  assign not_1_out = ~B;  // NOT_Gate not_1, 32 bits wide
  // CPA cpa_1: pin names not known; wires that end beside it: multiplexer_1_out, A
  // Pins of 1 and 3 bits meet at ALUControl
endmodule
