// Logisim project Arch_EVM222.circ as structural Verilog
module HalfAdder (
  input  a,
  input  b,
  output s,
  output carry
);

  and and_1 (carry, a, b);
  xor xor_1 (s, a, b);
endmodule

module FullAdder (
  input  Cin,
  input  a,
  input  b,
  output s,
  output Cout
);

  wire halfadder_1_carry, halfadder_1_s, halfadder_2_carry;

  HalfAdder halfadder_1 (.a(a), .b(b), .s(halfadder_1_s), .carry(halfadder_1_carry));
  HalfAdder halfadder_2 (.a(Cin), .b(halfadder_1_s), .s(s), .carry(halfadder_2_carry));
  or or_1 (Cout, halfadder_2_carry, halfadder_1_carry);
endmodule

module CPA (
  input  Cin,
  input  [3:0] a,
  input  [3:0] b,
  output [3:0] S,
  output Cout
);

  wire fulladder_1_cout, fulladder_2_cout, fulladder_3_cout;

  FullAdder fulladder_1 (.Cin(Cin), .a(a[0]), .b(b[0]), .s(S[0]), .Cout(fulladder_1_cout));
  FullAdder fulladder_2 (.Cin(fulladder_1_cout), .a(a[1]), .b(b[1]), .s(S[1]), .Cout(fulladder_2_cout));
  FullAdder fulladder_3 (.Cin(fulladder_2_cout), .a(a[2]), .b(b[2]), .s(S[2]), .Cout(fulladder_3_cout));
  FullAdder fulladder_4 (.Cin(fulladder_3_cout), .a(a[3]), .b(b[3]), .s(S[3]), .Cout(Cout));
endmodule

module Incrementer (
  input  Cin,
  input  [3:0] a,
  output [3:0] out_3
);

  CPA cpa_1 (.Cin(Cin), .a(a), .b(4'b0001), .S(out_3));  // open: Cout
endmodule

module Sub (
  input  Cin,
  input  [3:0] a,
  input  [3:0] b,
  output [3:0] S,
  output Cout
);

  wire [3:0] not_1_out;

  assign not_1_out = ~b;  // NOT_Gate not_1, 4 bits wide
  CPA cpa_1 (.Cin(Cin), .a(a), .b(not_1_out), .S(S), .Cout(Cout));
endmodule

module SubSum (
  input  K,
  input  [3:0] b,
  input  [3:0] a,
  output Cout,
  output [3:0] S
);

  wire [3:0] multiplexer_1_out, not_1_out;

  assign not_1_out = ~b;  // NOT_Gate not_1, 4 bits wide
  Multiplexer #(.width(4)) multiplexer_1 (.in0(b), .in1(not_1_out), .out(multiplexer_1_out), .sel(K));
  CPA cpa_1 (.Cin(K), .a(multiplexer_1_out), .b(a), .S(S), .Cout(Cout));
endmodule

module OverFlow (
  input  K,
  input  [3:0] b,
  input  [3:0] a,
  output V,
  output [3:0] S
);

  wire xnor_1_out, xor_1_out;
  wire [3:0] multiplexer_1_out, not_1_out;

  assign not_1_out = ~b;  // NOT_Gate not_1, 4 bits wide
  Multiplexer #(.width(4)) multiplexer_1 (.in0(b), .in1(not_1_out), .out(multiplexer_1_out), .sel(K));
  CPA cpa_1 (.Cin(K), .a(multiplexer_1_out), .b(a), .S(S));  // open: Cout
  xnor xnor_1 (xnor_1_out, multiplexer_1_out[3], a[3]);
  xor xor_1 (xor_1_out, a[3], S[3]);
  and and_1 (V, xnor_1_out, xor_1_out);
endmodule

module Comparators (
  input  [3:0] a,
  input  [3:0] b,
  output Equal
);

  wire and_1_out, and_2_out, xnor_1_out, xnor_2_out, xnor_3_out, xnor_4_out;

  xnor xnor_1 (xnor_1_out, a[0], b[0]);
  xnor xnor_2 (xnor_2_out, a[1], b[1]);
  xnor xnor_3 (xnor_3_out, a[2], b[2]);
  xnor xnor_4 (xnor_4_out, a[3], b[3]);
  and and_1 (and_1_out, xnor_3_out, xnor_4_out);
  and and_2 (and_2_out, xnor_1_out, xnor_2_out);
  and and_3 (Equal, and_2_out, and_1_out);
endmodule

module Comparators2 (
  input  [3:0] a,
  input  [3:0] b,
  output out_3
);

  wire not_1_out;
  wire [3:0] sub_1_s;

  Sub sub_1 (.Cin(1'b1), .a(b), .b(a), .S(sub_1_s));  // open: Cout
  not not_1 (not_1_out, sub_1_s[0]);
  and and_1 (out_3, not_1_out, 1'b1);
endmodule

module SintComp (
  input  [3:0] a,
  input  [3:0] b,
  output neq,
  output eq,
  output lte,
  output gt,
  output gte,
  output lt
);

  Comparators comparators_1 (.a(a), .b(b), .Equal(eq));
  Comparators2 comparators2_1 (.a(a), .b(b), .out_3(gt));
  Comparators2 comparators2_2 (.a(a), .b(b), .out_3(lt));
  not not_1 (neq, eq);
  not not_2 (lte, gt);
  not not_3 (gte, lt);
endmodule

module ALU (
  input  [2:0] ALUControl,
  input  [31:0] B,
  input  [31:0] A,
  output [31:0] S,
  output out_5,
  output out_6,
  output [4:0] out_7,
  output [31:0] out_8,
  output out_9
);

  wire bitselector_1_out;
  wire [31:0] and_1_out, bit_extender_1_out, multiplexer_1_out, not_1_out, or_1_out;

  Multiplexer #(.width(32)) multiplexer_1 (.in0(B), .in1(not_1_out), .out(multiplexer_1_out), .sel(ALUControl[2]));
  assign not_1_out = ~B;  // NOT_Gate not_1, 32 bits wide
  Adder #(.width(32)) adder_1 (.a(multiplexer_1_out), .b(A), .out(out_8), .cin(ALUControl[2]));  // open: cout
  assign and_1_out = multiplexer_1_out & A;  // AND_Gate and_1, 32 bits wide
  assign or_1_out = multiplexer_1_out | A;  // OR_Gate or_1, 32 bits wide
  BitSelector #(.width(32)) bitselector_1 (.in(out_8), .out(bitselector_1_out), .sel(out_7));
  assign bit_extender_1_out = {{31{1'b0}}, bitselector_1_out};  // Bit_Extender bit_extender_1
  Multiplexer #(.select(2), .width(32)) multiplexer_2 (
    .in0(and_1_out), .in1(or_1_out), .in2(out_8), .in3(bit_extender_1_out), .out(S), .sel(ALUControl[1:0]));
  Zero zero_1 (.in_1(S), .out_2(out_5));
  Negative negative_1 (.in_1(S), .out_3(out_6));  // open: in_2
  OverFlow32 overflow32_1 (.A(A), .B(multiplexer_1_out), .S(S), .out_4(out_9));
endmodule

module Or32 (
  input  [31:0] A,
  output S
);

  wire or_1_out, or_2_out, or_3_out, or_4_out, or_5_out, or_6_out, or_7_out, or_8_out, or_9_out, or_10_out,
       or_11_out, or_12_out, or_13_out, or_14_out, or_15_out, or_16_out, or_17_out, or_18_out, or_19_out,
       or_20_out, or_21_out, or_22_out, or_23_out, or_24_out, or_25_out, or_26_out, or_27_out, or_28_out,
       or_29_out, or_30_out;

  or or_1 (or_1_out, A[0], A[1]);
  or or_2 (or_2_out, A[2], A[3]);
  or or_3 (or_3_out, A[4], A[5]);
  or or_4 (or_4_out, A[6], A[7]);
  or or_5 (or_5_out, A[8], A[9]);
  or or_6 (or_6_out, A[10], A[11]);
  or or_7 (or_7_out, A[12], A[13]);
  or or_8 (or_8_out, A[14], A[15]);
  or or_9 (or_9_out, A[16], A[17]);
  or or_10 (or_10_out, A[18], A[19]);
  or or_11 (or_11_out, A[20], A[21]);
  or or_12 (or_12_out, A[22], A[23]);
  or or_13 (or_13_out, A[24], A[25]);
  or or_14 (or_14_out, A[26], A[27]);
  or or_15 (or_15_out, A[28], A[29]);
  or or_16 (or_16_out, A[30], A[31]);
  or or_17 (or_17_out, or_1_out, or_2_out);
  or or_18 (or_18_out, or_3_out, or_4_out);
  or or_19 (or_19_out, or_5_out, or_6_out);
  or or_20 (or_20_out, or_7_out, or_8_out);
  or or_21 (or_21_out, or_9_out, or_10_out);
  or or_22 (or_22_out, or_11_out, or_12_out);
  or or_23 (or_23_out, or_13_out, or_14_out);
  or or_24 (or_24_out, or_15_out, or_16_out);
  or or_25 (or_25_out, or_17_out, or_18_out);
  or or_26 (or_26_out, or_19_out, or_20_out);
  or or_27 (or_27_out, or_21_out, or_22_out);
  or or_28 (or_28_out, or_23_out, or_24_out);
  or or_29 (or_29_out, or_25_out, or_26_out);
  or or_30 (or_30_out, or_27_out, or_28_out);
  or or_31 (S, or_29_out, or_30_out);
endmodule

module Zero (
  input  [31:0] in_1,
  output out_2
);

  wire or32_1_s;

  not not_1 (out_2, or32_1_s);
  Or32 or32_1 (.A(in_1), .S(or32_1_s));
endmodule

module Negative (
  input  [31:0] in_1,
  input  [4:0] in_2,
  output out_3
);

  BitSelector #(.width(32)) bitselector_1 (.in(in_1), .out(out_3), .sel(in_2));
endmodule

module OverFlow32 (
  input  [31:0] A,
  input  [31:0] B,
  input  [31:0] S,
  output out_4
);

  wire xnor_1_out, xor_1_out;

  xnor xnor_1 (xnor_1_out, A[31], B[31]);
  xor xor_1 (xor_1_out, A[31], S[31]);
  and and_1 (out_4, xnor_1_out, xor_1_out);
endmodule

module My_Shifter (
  input  [1:0] in_1,
  input  [3:0] in_2,
  output [3:0] out_3
);

  Multiplexer #(.select(2)) multiplexer_1 (
    .in0(in_2[3]), .in1(in_2[2]), .in2(in_2[1]), .in3(in_2[0]), .out(out_3[0]), .sel(in_1));
  Multiplexer #(.select(2)) multiplexer_2 (
    .in0(in_2[2]), .in1(in_2[1]), .in2(in_2[0]), .in3(in_2[0]), .out(out_3[1]), .sel(in_1));
  Multiplexer #(.select(2)) multiplexer_3 (
    .in0(in_2[1]), .in1(in_2[0]), .in2(in_2[0]), .in3(in_2[0]), .out(out_3[2]), .sel(in_1));
  Multiplexer #(.select(2)) multiplexer_4 (
    .in0(in_2[0]), .in1(in_2[0]), .in2(in_2[0]), .in3(in_2[0]), .out(out_3[3]), .sel(in_1));
endmodule

module My_Shifter2 (
  input  [1:0] in_1,
  input  [3:0] A,
  output [3:0] out_3
);

  Multiplexer #(.select(2)) multiplexer_1 (.in0(A[3]), .out(out_3[0]), .sel(in_1));  // open: in1, in2, in3
  Multiplexer #(.select(2)) multiplexer_2 (.in0(A[2]), .in1(A[3]), .out(out_3[1]), .sel(in_1));  // open: in2, in3
  Multiplexer #(.select(2)) multiplexer_3 (
    .in0(A[2]), .in1(A[2]), .in2(A[3]), .out(out_3[2]), .sel(in_1));  // open: in3
  Multiplexer #(.select(2)) multiplexer_4 (.in0(A[2]), .in1(A[2]), .in2(A[2]), .in3(A[3]), .out(out_3[3]), .sel(in_1));

  assign A[1:0] = {2{A[2]}};
endmodule
