// Logisim project Architecture.circ as structural Verilog: 16 circuits, main circuit main
module main (
  input  in_1,
  input  in_2,
  input  in_3,
  input  in_4,
  input  in_5,
  input  in_6,
  input  in_7,
  input  in_8,
  input  in_9,
  input  in_10,
  input  in_11,
  input  in_12,
  input  [3:0] in_13,
  input  [3:0] in_14,
  input  [3:0] in_15,
  input  [3:0] in_16,
  input  [3:0] in_17,
  input  [3:0] in_18,
  input  [3:0] in_19,
  input  in_20,
  input  [7:0] in_21,
  input  in_22,
  input  [3:0] in_23,
  input  [3:0] in_24,
  input  in_25,
  input  [3:0] in_26,
  input  [3:0] in_27,
  input  [3:0] in_28,
  input  [3:0] in_29,
  input  [3:0] in_30,
  input  [3:0] in_31,
  input  [3:0] in_32,
  input  [3:0] in_33,
  input  [3:0] in_34,
  input  [3:0] in_35,
  input  [2:0] in_36,
  input  [7:0] in_37,
  input  in_38,
  input  in_39,
  input  [7:0] in_40,
  input  in_41,
  input  in_42,
  input  in_43,
  output out_44,
  output out_45,
  output out_46,
  output out_47,
  output out_48,
  output out_49,
  output out_50,
  output [3:0] out_51,
  output [3:0] out_52,
  output out_53,
  output [3:0] out_54,
  output out_55,
  output [3:0] out_56,
  output [3:0] out_57,
  output out_58,
  output out_59,
  output out_60,
  output out_61,
  output out_62,
  output out_63,
  output out_64,
  output out_65,
  output out_66,
  output out_67,
  output out_68,
  output out_69
);

  my_not my_not_1 (.a(in_1), .out_2(out_44));
  my_and my_and_1 (.x(in_2), .y(in_3), .out_3(out_45));
  my_or my_or_1 (.in_1(in_4), .in_2(in_5), .out_3(out_46));
  my_Xor my_xor_1 (.in_1(in_6), .in_2(in_7), .out_3(out_47));
  my_MUX my_mux_1 (.a(in_8), .sel(in_9), .b(in_10), .out_4(out_48));
  my_DMux my_dmux_1 (.i_n(in_11), .sel(in_12), .out_3(out_49), .out_4(out_50));
  my_Not4 my_not4_1 (.in_1(in_13), .out_2(out_51));
  my_And4 my_and4_1 (.in_1(in_14), .in_2(in_15), .out_3(out_52));
  my_Or4 my_or4_1 (.in_1(in_16), .in_2(in_17), .out_3(out_53));
  my_MUX4 my_mux4_1 (.a(in_18), .b(in_19), .sel(in_20), .out_4(out_54));
  Mux4Way4 mux4way4_1 (.sel2(in_22), .a(in_23), .b(in_24), .sel1(in_25), .c(in_26), .d(in_27), .out_7(out_56));
  My_OR8Way my_or8way_1 (.in_1(in_21), .out_2(out_55));
  Mux8Way4 mux8way4_1 (
    .a(in_28), .b(in_29), .c(in_30), .d(in_31), .e(in_32), .f(in_33), .g(in_34), .h(in_35), .sel3(in_36),
    .out_10(out_57));
  // DMux4 dmux4_1: pin names not known; wires that end beside it: in_38, in_39, in_37, out_58, out_59, out_60, out_61
  // DMux8 dmux8_1: pin names not known; wires that end beside it: in_41, in_42, in_43, in_40, out_62, out_63, out_64, out_65, out_66, out_67, out_68, out_69
endmodule

module my_not (
  input  a,
  output out_2
);

  nand nand_1 (out_2, a, a);
endmodule

module my_and (
  input  x,
  input  y,
  output out_3
);

  wire nand_1_out;

  nand nand_1 (nand_1_out, x, y);
  my_not my_not_1 (.a(nand_1_out), .out_2(out_3));
endmodule

module my_or (
  input  in_1,
  input  in_2,
  output out_3
);

  wire my_and_1_out_3, my_not_1_out_2, my_not_2_out_2;

  my_not my_not_1 (.a(in_1), .out_2(my_not_1_out_2));
  my_not my_not_2 (.a(in_2), .out_2(my_not_2_out_2));
  my_and my_and_1 (.x(my_not_1_out_2), .y(my_not_2_out_2), .out_3(my_and_1_out_3));
  my_not my_not_3 (.a(my_and_1_out_3), .out_2(out_3));
endmodule

module my_Xor (
  input  in_1,
  input  in_2,
  output out_3
);

  wire my_and_1_out_3, my_and_2_out_3, my_not_1_out_2, my_not_2_out_2;

  my_not my_not_1 (.a(in_2), .out_2(my_not_1_out_2));
  my_not my_not_2 (.a(in_1), .out_2(my_not_2_out_2));
  my_and my_and_1 (.x(in_1), .y(my_not_1_out_2), .out_3(my_and_1_out_3));
  my_and my_and_2 (.x(my_not_2_out_2), .y(in_2), .out_3(my_and_2_out_3));
  my_or my_or_1 (.in_1(my_and_1_out_3), .in_2(my_and_2_out_3), .out_3(out_3));
endmodule

module my_MUX (
  input  a,
  input  sel,
  input  b,
  output out_4
);

  wire my_and_1_out_3, my_and_2_out_3, my_not_1_out_2;

  my_not my_not_1 (.a(sel), .out_2(my_not_1_out_2));
  my_and my_and_1 (.x(a), .y(sel), .out_3(my_and_1_out_3));
  my_and my_and_2 (.x(my_not_1_out_2), .y(b), .out_3(my_and_2_out_3));
  my_or my_or_1 (.in_1(my_and_1_out_3), .in_2(my_and_2_out_3), .out_3(out_4));
endmodule

module my_DMux (
  input  i_n,
  input  sel,
  output out_3,
  output out_4
);

  wire my_not_1_out_2;

  my_not my_not_1 (.a(sel), .out_2(my_not_1_out_2));
  my_and my_and_1 (.x(i_n), .y(sel), .out_3(out_3));
  my_and my_and_2 (.x(i_n), .y(my_not_1_out_2), .out_3(out_4));
endmodule

module my_Not4 (
  input  [3:0] in_1,
  output [3:0] out_2
);

  my_not my_not_1 (.a(in_1[0]), .out_2(out_2[0]));
  my_not my_not_2 (.a(in_1[1]), .out_2(out_2[1]));
  my_not my_not_3 (.a(in_1[2]), .out_2(out_2[2]));
  my_not my_not_4 (.a(in_1[3]), .out_2(out_2[3]));
endmodule

module my_And4 (
  input  [3:0] in_1,
  input  [3:0] in_2,
  output [3:0] out_3
);

  my_and my_and_1 (.x(in_1[0]), .y(in_2[0]), .out_3(out_3[0]));
  my_and my_and_2 (.x(in_1[1]), .y(in_2[1]), .out_3(out_3[1]));
  my_and my_and_3 (.x(in_1[2]), .y(in_2[2]), .out_3(out_3[2]));
  my_and my_and_4 (.x(in_1[3]), .y(in_2[3]), .out_3(out_3[3]));
endmodule

module my_Or4 (
  input  [3:0] in_1,
  input  [3:0] in_2,
  output out_3
);

  wire my_or_1_out_3, my_or_2_out_3, my_or_3_out_3, my_or_4_out_3, my_or_5_p3, my_or_6_out_3;

  my_or my_or_1 (.in_1(in_1[0]), .in_2(in_2[0]), .out_3(my_or_1_out_3));
  my_or my_or_2 (.in_1(in_1[1]), .in_2(in_2[1]), .out_3(my_or_2_out_3));
  my_or my_or_3 (.in_1(in_1[2]), .in_2(in_2[2]), .out_3(my_or_3_out_3));
  my_or my_or_4 (.in_1(in_1[3]), .in_2(in_2[3]), .out_3(my_or_4_out_3));
  // my_or my_or_5: pin names not known; wires that end beside it: my_or_1_out_3, my_or_2_out_3, my_or_5_p3
  my_or my_or_6 (.in_1(my_or_3_out_3), .in_2(my_or_4_out_3), .out_3(my_or_6_out_3));
  my_or my_or_7 (.in_1(my_or_5_p3), .in_2(my_or_6_out_3), .out_3(out_3));
endmodule

module my_MUX4 (
  input  [3:0] a,
  input  [3:0] b,
  input  sel,
  output [3:0] out_4
);

  my_MUX my_mux_1 (.a(a[0]), .sel(sel), .b(b[0]), .out_4(out_4[0]));
  my_MUX my_mux_2 (.a(a[1]), .sel(sel), .b(b[1]), .out_4(out_4[1]));
  my_MUX my_mux_3 (.a(a[2]), .sel(sel), .b(b[2]), .out_4(out_4[2]));
  my_MUX my_mux_4 (.a(a[3]), .sel(sel), .b(b[3]), .out_4(out_4[3]));
endmodule

module My_OR8Way (
  input  [7:0] in_1,
  output out_2
);

  wire my_or_1_out_3, my_or_2_out_3, my_or_3_out_3, my_or_4_out_3, my_or_5_out_3, my_or_6_out_3;

  my_or my_or_1 (.in_1(in_1[0]), .in_2(in_1[1]), .out_3(my_or_1_out_3));
  my_or my_or_2 (.in_1(in_1[2]), .in_2(in_1[3]), .out_3(my_or_2_out_3));
  my_or my_or_3 (.in_1(in_1[4]), .in_2(in_1[5]), .out_3(my_or_3_out_3));
  my_or my_or_4 (.in_1(in_1[6]), .in_2(in_1[7]), .out_3(my_or_4_out_3));
  my_or my_or_5 (.in_1(my_or_1_out_3), .in_2(my_or_2_out_3), .out_3(my_or_5_out_3));
  my_or my_or_6 (.in_1(my_or_3_out_3), .in_2(my_or_4_out_3), .out_3(my_or_6_out_3));
  my_or my_or_7 (.in_1(my_or_5_out_3), .in_2(my_or_6_out_3), .out_3(out_2));
endmodule

module Mux4Way4 (
  input  sel2,
  input  [3:0] a,
  input  [3:0] b,
  input  sel1,
  input  [3:0] c,
  input  [3:0] d,
  output [3:0] out_7
);

  wire [3:0] my_mux4_1_out_4, my_mux4_2_out_4;

  my_MUX4 my_mux4_1 (.a(a), .b(b), .sel(sel1), .out_4(my_mux4_1_out_4));
  my_MUX4 my_mux4_2 (.a(c), .b(d), .sel(sel1), .out_4(my_mux4_2_out_4));
  my_MUX4 my_mux4_3 (.a(my_mux4_1_out_4), .b(my_mux4_2_out_4), .sel(sel2), .out_4(out_7));
endmodule

module Mux8Way4 (
  input  [3:0] a,
  input  [3:0] b,
  input  [3:0] c,
  input  [3:0] d,
  input  [3:0] e,
  input  [3:0] f,
  input  [3:0] g,
  input  [3:0] h,
  input  [2:0] sel3,
  output [3:0] out_10
);

  wire [3:0] my_mux4_1_out_4, my_mux4_2_out_4, my_mux4_3_out_4, my_mux4_4_out_4, my_mux4_5_out_4,
       my_mux4_6_out_4;

  my_MUX4 my_mux4_1 (.a(a), .b(b), .sel(sel3[0]), .out_4(my_mux4_1_out_4));
  my_MUX4 my_mux4_2 (.a(c), .b(d), .sel(sel3[0]), .out_4(my_mux4_2_out_4));
  my_MUX4 my_mux4_3 (.a(e), .b(f), .sel(sel3[0]), .out_4(my_mux4_3_out_4));
  my_MUX4 my_mux4_4 (.a(g), .b(h), .sel(sel3[0]), .out_4(my_mux4_4_out_4));
  my_MUX4 my_mux4_5 (.a(my_mux4_1_out_4), .b(my_mux4_2_out_4), .sel(sel3[1]), .out_4(my_mux4_5_out_4));
  my_MUX4 my_mux4_6 (.a(my_mux4_3_out_4), .b(my_mux4_4_out_4), .sel(sel3[1]), .out_4(my_mux4_6_out_4));
  my_MUX4 my_mux4_7 (.a(my_mux4_5_out_4), .b(my_mux4_6_out_4), .sel(sel3[2]), .out_4(out_10));
endmodule

module DMux4 (
  input  a,
  input  sel1,
  input  sel2,
  output out_4,
  output out_5,
  output out_6,
  output out_7
);

  wire my_dmux_1_out_3, my_dmux_1_out_4;

  my_DMux my_dmux_1 (.i_n(a), .sel(sel1), .out_3(my_dmux_1_out_3), .out_4(my_dmux_1_out_4));
  my_DMux my_dmux_2 (.i_n(my_dmux_1_out_3), .sel(sel2), .out_3(out_4), .out_4(out_5));
  my_DMux my_dmux_3 (.i_n(my_dmux_1_out_4), .sel(sel2), .out_3(out_6), .out_4(out_7));
endmodule

module DMux8 (
  input  a,
  input  sel1,
  input  sel2,
  input  sel3,
  output out_5,
  output out_6,
  output out_7,
  output out_8,
  output out_9,
  output out_10,
  output out_11,
  output out_12
);

  wire my_dmux_1_out_3, my_dmux_1_out_4, my_dmux_2_out_3, my_dmux_2_out_4, my_dmux_3_out_3, my_dmux_3_out_4;

  my_DMux my_dmux_1 (.i_n(a), .sel(sel1), .out_3(my_dmux_1_out_3), .out_4(my_dmux_1_out_4));
  my_DMux my_dmux_2 (.i_n(my_dmux_1_out_3), .sel(sel2), .out_3(my_dmux_2_out_3), .out_4(my_dmux_2_out_4));
  my_DMux my_dmux_3 (.i_n(my_dmux_1_out_4), .sel(sel2), .out_3(my_dmux_3_out_3), .out_4(my_dmux_3_out_4));
  my_DMux my_dmux_4 (.i_n(my_dmux_2_out_3), .sel(sel3), .out_3(out_5), .out_4(out_6));
  my_DMux my_dmux_5 (.i_n(my_dmux_2_out_4), .sel(sel3), .out_3(out_7), .out_4(out_8));
  my_DMux my_dmux_6 (.i_n(my_dmux_3_out_3), .sel(sel3), .out_3(out_9), .out_4(out_10));
  my_DMux my_dmux_7 (.i_n(my_dmux_3_out_4), .sel(sel3), .out_3(out_11), .out_4(out_12));
endmodule
