// Logisim project praktika_gotovaya.circ as structural Verilog: 16 circuits, main circuit main
module main (
  input  a,
  input  x,
  input  y,
  input  x1,
  input  y1,
  input  x2,
  input  y2,
  input  b1,
  input  sel,
  input  a1,
  input  vxod,
  input  sel1,
  input  [3:0] vxod1,
  input  [3:0] x3,
  input  [3:0] y3,
  input  [3:0] x4,
  input  [3:0] y4,
  input  [3:0] x5,
  input  [3:0] y5,
  input  sel2,
  input  [7:0] ln,
  input  [3:0] in_22,
  input  [3:0] in_23,
  input  in_24,
  input  [3:0] in_25,
  input  [3:0] in_26,
  input  in_27,
  input  [3:0] in_28,
  input  [3:0] in_29,
  input  in_30,
  input  [3:0] in_31,
  input  in_32,
  input  [3:0] in_33,
  input  in_34,
  input  [3:0] in_35,
  input  [3:0] in_36,
  input  [3:0] in_37,
  input  [3:0] in_38,
  input  in_39,
  input  in_40,
  input  in_41,
  input  in_42,
  input  in_43,
  input  in_44,
  input  in_45,
  output vixod,
  output vixod1,
  output vixod2,
  output vixod3,
  output vixod4,
  output b2,
  output a2,
  output [3:0] vixod5,
  output [3:0] vixod6,
  output [3:0] vixod7,
  output [3:0] vixod8,
  output vixod9,
  output [3:0] out_58,
  output [3:0] out_59,
  output [3:0] out_60,
  output [7:0] out_61
);

  my_not my_not_1 (.a(a), .y(vixod));
  my_and my_and_1 (.x(x), .y(y), .vixod(vixod1));
  my_or my_or_1 (.x(x1), .y(y1), .vixod(vixod2));
  my_xor my_xor_1 (.a(x2), .b(y2), .vixod(vixod3));
  my_mux my_mux_1 (.b(b1), .sel(sel), .a(a1), .vixod(vixod4));
  my_dmux my_dmux_1 (.vxod(vxod), .sel(sel1), .b(b2), .a(a2));
  my_not4 my_not4_1 (.in_1(vxod1), .out_2(vixod5));
  my_and4 my_and4_1 (.x(x3), .y(y3), .out_3(vixod6));
  my_or4 my_or4_1 (.x(x4), .y(y4), .vixod(vixod7));
  my_mux4 my_mux4_1 (.a(x5), .b(y5), .sel(sel2), .out_4(vixod8));
  or8way or8way_1 (.in_1(ln), .out_2(vixod9));
  my_mux4way4 my_mux4way4_1 (
    .x1(in_22), .x2(in_23), .sel1(in_24), .x3(in_25), .x4(in_26), .sel2(in_27), .out_7(out_58));
  my_mux8way4 my_mux8way4_1 (
    .x1(in_28), .x2(in_29), .sel1(in_30), .x3(in_31), .sel2(in_32), .x4(in_33), .x5(in_35), .sel3(in_34),
    .x6(in_36), .x7(in_37), .x8(in_38), .out_12(out_59));
  my_dmux4 my_dmux4_1 (
    .ln(in_39), .sel1(in_40), .sel2(in_41), .out_4(out_60[0]), .out_5(out_60[1]), .out_6(out_60[2]),
    .out_7(out_60[3]));
  my_dmux8 my_dmux8_1 (
    .ln(in_42), .sel1(in_43), .sel2(in_44), .sel3(in_45), .out_5(out_61[0]), .out_6(out_61[1]),
    .out_7(out_61[2]), .out_8(out_61[3]), .out_9(out_61[4]), .out_10(out_61[5]), .out_11(out_61[6]),
    .out_12(out_61[7]));
endmodule

module my_not (
  input  a,
  output y
);

  nand nand_1 (y, a, a);
endmodule

module my_and (
  input  x,
  input  y,
  output vixod
);

  wire nand_1_out;

  nand nand_1 (nand_1_out, x, y);
  my_not my_not_1 (.a(nand_1_out), .y(vixod));
endmodule

module my_or (
  input  x,
  input  y,
  output vixod
);

  wire my_and_1_vixod, my_not_1_y, my_not_2_y;

  my_not my_not_1 (.a(x), .y(my_not_1_y));
  my_not my_not_2 (.a(y), .y(my_not_2_y));
  my_and my_and_1 (.x(my_not_1_y), .y(my_not_2_y), .vixod(my_and_1_vixod));
  my_not my_not_3 (.a(my_and_1_vixod), .y(vixod));
endmodule

module my_xor (
  input  a,
  input  b,
  output vixod
);

  wire my_and_1_vixod, my_and_2_vixod, my_not_1_y, my_not_2_y;

  my_not my_not_1 (.a(b), .y(my_not_1_y));
  my_not my_not_2 (.a(a), .y(my_not_2_y));
  my_and my_and_1 (.x(a), .y(my_not_1_y), .vixod(my_and_1_vixod));
  my_and my_and_2 (.x(my_not_2_y), .y(b), .vixod(my_and_2_vixod));
  my_or my_or_1 (.x(my_and_1_vixod), .y(my_and_2_vixod), .vixod(vixod));
endmodule

module my_mux (
  input  b,
  input  sel,
  input  a,
  output vixod
);

  wire my_and_1_vixod, my_and_2_vixod, my_not_1_y;

  my_not my_not_1 (.a(sel), .y(my_not_1_y));
  my_and my_and_1 (.x(b), .y(sel), .vixod(my_and_1_vixod));
  my_and my_and_2 (.x(a), .y(my_not_1_y), .vixod(my_and_2_vixod));
  my_or my_or_1 (.x(my_and_1_vixod), .y(my_and_2_vixod), .vixod(vixod));
endmodule

module my_dmux (
  input  vxod,
  input  sel,
  output b,
  output a
);

  wire my_not_1_y;

  my_not my_not_1 (.a(sel), .y(my_not_1_y));
  my_and my_and_1 (.x(sel), .y(vxod), .vixod(b));
  my_and my_and_2 (.x(vxod), .y(my_not_1_y), .vixod(a));
endmodule

module my_not4 (
  input  [3:0] in_1,
  output [3:0] out_2
);

  my_not my_not_1 (.a(in_1[0]), .y(out_2[0]));
  my_not my_not_2 (.a(in_1[1]), .y(out_2[1]));
  my_not my_not_3 (.a(in_1[2]), .y(out_2[2]));
  my_not my_not_4 (.a(in_1[3]), .y(out_2[3]));
endmodule

module my_and4 (
  input  [3:0] x,
  input  [3:0] y,
  output [3:0] out_3
);

  my_and my_and_1 (.x(x[0]), .y(y[0]), .vixod(out_3[0]));
  my_and my_and_2 (.x(x[1]), .y(y[1]), .vixod(out_3[1]));
  my_and my_and_3 (.x(x[2]), .y(y[2]), .vixod(out_3[2]));
  my_and my_and_4 (.x(x[3]), .y(y[3]), .vixod(out_3[3]));
endmodule

module my_or4 (
  input  [3:0] x,
  input  [3:0] y,
  output [3:0] vixod
);

  my_or my_or_1 (.x(x[0]), .y(y[0]), .vixod(vixod[0]));
  my_or my_or_2 (.x(x[1]), .y(y[1]), .vixod(vixod[1]));
  my_or my_or_3 (.x(x[2]), .y(y[2]), .vixod(vixod[2]));
  my_or my_or_4 (.x(x[3]), .y(y[3]), .vixod(vixod[3]));
endmodule

module my_mux4 (
  input  [3:0] a,
  input  [3:0] b,
  input  sel,
  output [3:0] out_4
);

  my_mux my_mux_1 (.b(b[0]), .sel(sel), .a(a[0]), .vixod(out_4[0]));
  my_mux my_mux_2 (.b(b[1]), .sel(sel), .a(a[1]), .vixod(out_4[1]));
  my_mux my_mux_3 (.b(b[2]), .sel(sel), .a(a[2]), .vixod(out_4[2]));
  my_mux my_mux_4 (.b(b[3]), .sel(sel), .a(a[3]), .vixod(out_4[3]));
endmodule

module my_mux4way4 (
  input  [3:0] x1,
  input  [3:0] x2,
  input  sel1,
  input  [3:0] x3,
  input  [3:0] x4,
  input  sel2,
  output [3:0] out_7
);

  wire [3:0] my_mux4_1_out_4, my_mux4_2_out_4;

  my_mux4 my_mux4_1 (.a(x1), .b(x2), .sel(sel1), .out_4(my_mux4_1_out_4));
  my_mux4 my_mux4_2 (.a(x3), .b(x4), .sel(sel1), .out_4(my_mux4_2_out_4));
  my_mux4 my_mux4_3 (.a(my_mux4_1_out_4), .b(my_mux4_2_out_4), .sel(sel2), .out_4(out_7));
endmodule

module my_mux8way4 (
  input  [3:0] x1,
  input  [3:0] x2,
  input  sel1,
  input  [3:0] x3,
  input  sel2,
  input  [3:0] x4,
  input  [3:0] x5,
  input  sel3,
  input  [3:0] x6,
  input  [3:0] x7,
  input  [3:0] x8,
  output [3:0] out_12
);

  wire [3:0] my_mux4way4_1_out_7, my_mux4way4_2_out_7;

  my_mux4way4 my_mux4way4_1 (.x1(x1), .x2(x2), .sel1(sel1), .x3(x3), .x4(x4), .sel2(sel2), .out_7(my_mux4way4_1_out_7));
  my_mux4way4 my_mux4way4_2 (.x1(x5), .x2(x6), .sel1(sel1), .x3(x7), .x4(x8), .sel2(sel2), .out_7(my_mux4way4_2_out_7));
  my_mux4 my_mux4_1 (.a(my_mux4way4_1_out_7), .b(my_mux4way4_2_out_7), .sel(sel3), .out_4(out_12));
endmodule

module my_dmux4 (
  input  ln,
  input  sel1,
  input  sel2,
  output out_4,
  output out_5,
  output out_6,
  output out_7
);

  wire my_dmux_1_a, my_dmux_1_b;

  my_dmux my_dmux_1 (.vxod(ln), .sel(sel1), .b(my_dmux_1_b), .a(my_dmux_1_a));
  my_dmux my_dmux_2 (.vxod(my_dmux_1_b), .sel(sel2), .b(out_4), .a(out_5));
  my_dmux my_dmux_3 (.vxod(my_dmux_1_a), .sel(sel2), .b(out_6), .a(out_7));
endmodule

module my_dmux8 (
  input  ln,
  input  sel1,
  input  sel2,
  input  sel3,
  output out_5,
  output out_6,
  output out_7,
  output out_8,
  output out_9,
  output out_10,
  output out_11,
  output out_12
);

  wire my_dmux_1_a, my_dmux_1_b;

  my_dmux my_dmux_1 (.vxod(ln), .sel(sel1), .b(my_dmux_1_b), .a(my_dmux_1_a));
  my_dmux4 my_dmux4_1 (
    .ln(my_dmux_1_b), .sel1(sel2), .sel2(sel3), .out_4(out_5), .out_5(out_6), .out_6(out_7), .out_7(out_8));
  my_dmux4 my_dmux4_2 (
    .ln(my_dmux_1_a), .sel1(sel2), .sel2(sel3), .out_4(out_9), .out_5(out_10), .out_6(out_11), .out_7(out_12));
endmodule

module or8way (
  input  [7:0] in_1,
  output out_2
);

  wire my_or_1_vixod, my_or_2_vixod, my_or_3_vixod, my_or_4_vixod, my_or_5_vixod, my_or_6_vixod;

  my_or my_or_1 (.x(in_1[0]), .y(in_1[1]), .vixod(my_or_1_vixod));
  my_or my_or_2 (.x(in_1[2]), .y(in_1[3]), .vixod(my_or_2_vixod));
  my_or my_or_3 (.x(in_1[4]), .y(in_1[5]), .vixod(my_or_3_vixod));
  my_or my_or_4 (.x(in_1[6]), .y(in_1[7]), .vixod(my_or_4_vixod));
  my_or my_or_5 (.x(my_or_1_vixod), .y(my_or_2_vixod), .vixod(my_or_5_vixod));
  my_or my_or_6 (.x(my_or_3_vixod), .y(my_or_4_vixod), .vixod(my_or_6_vixod));
  my_or my_or_7 (.x(my_or_5_vixod), .y(my_or_6_vixod), .vixod(out_2));
endmodule
